# Fritzing sketch esp_rc (saved by Fritzing 0.9.5d)
breadboards: 1

parts:
  ESP1 = ESP32-DevkitC
  M1 = DC Motor
  M2 = DC Motor
  IC2 = IC, DIP package, 16 pins [chip_label="Driver TOP→"]
  IC1 = IC, SIP package, 3 pins [chip_label=3.3v]
  BATT1 = 3xAAA Switchable Battery Pack w/Bare Wire
  C1 = Electrolytic Capacitor [capacitance=0.47mF package="100 mil [THT, electrolytic]"]

nets:
  N1: ESP1.3V3, IC1.pin1
  N2: ESP1.GND, IC2.pin1, IC2.pin7, IC2.pin8, IC1.pin2, BATT1.NEG, C1.-
  N3: ESP1.IO19, IC2.pin5
  N4: ESP1.IO18, IC2.pin4
  N5: ESP1.IO17, IC2.pin3
  N6: ESP1.IO16, IC2.pin2
  N7: M1.pin_1, IC2.pin13
  N8: M1.pin_2, IC2.pin14
  N9: M2.pin_1, IC2.pin11
  N10: M2.pin_2, IC2.pin12
  N11: IC2.pin6, IC2.pin10, IC1.pin3, BATT1.POS, C1.+

custom parts:
  3xAAA Switchable Battery Pack w/Bare Wire: 3xAAA Switchable Battery Pack w/Bare Wire Connectors
